// Logisim project IE4756-arithmetic-logic-no-adder.circ as structural Verilog: 14 circuits, main circuit eq (4-bit)
module eq__4_bit (
  input  [3:0] in_1,
  input  [3:0] in_2,
  output out_3
);

  wire and_1_out, and_2_out, and_3_out, and_4_out, and_5_out, and_6_out, and_7_out, and_8_out, and_9_out,
       and_11_out, not_1_out, not_2_out, not_3_out, not_4_out, not_5_out, not_6_out, not_7_out, not_8_out,
       or_1_out, or_2_out, or_3_out, or_4_out;

  and and_1 (and_1_out, in_1[0], in_2[0]);
  not not_1 (not_1_out, in_1[0]);
  and and_2 (and_2_out, not_1_out, not_2_out);
  not not_2 (not_2_out, in_2[0]);
  and and_3 (and_3_out, in_1[1], in_2[1]);
  not not_3 (not_3_out, in_1[1]);
  and and_4 (and_4_out, not_3_out, not_4_out);
  not not_4 (not_4_out, in_2[1]);
  and and_5 (and_5_out, in_1[2], in_2[2]);
  not not_5 (not_5_out, in_1[2]);
  and and_6 (and_6_out, not_5_out, not_6_out);
  not not_6 (not_6_out, in_2[2]);
  and and_7 (and_7_out, in_1[3], in_2[3]);
  not not_7 (not_7_out, in_1[3]);
  and and_8 (and_8_out, not_7_out, not_8_out);
  not not_8 (not_8_out, in_2[3]);
  or or_1 (or_1_out, and_1_out, and_2_out);
  or or_2 (or_2_out, and_3_out, and_4_out);
  or or_3 (or_3_out, and_5_out, and_6_out);
  or or_4 (or_4_out, and_7_out, and_8_out);
  and and_9 (and_9_out, or_1_out, or_2_out);
  and and_10 (out_3, and_9_out, and_11_out);
  and and_11 (and_11_out, or_3_out, or_4_out);
endmodule

module eq__8_bit (
  input  [7:0] in_1,
  input  [7:0] in_2,
  output out_3
);

  wire eq_4_bit_1_out_3, eq_4_bit_2_out_3;

  eq__4_bit eq_4_bit_1 (.in_1(in_1[3:0]), .in_2(in_2[3:0]), .out_3(eq_4_bit_1_out_3));
  and and_1 (out_3, eq_4_bit_1_out_3, eq_4_bit_2_out_3);
  eq__4_bit eq_4_bit_2 (.in_1(in_1[7:4]), .in_2(in_2[7:4]), .out_3(eq_4_bit_2_out_3));
endmodule

module eq__32_bit (
  input  [31:0] in_1,
  input  [31:0] in_2,
  output out_3
);

  wire and_1_out, and_2_out, and_3_out, and_4_out, and_5_out, and_7_out, eq_4_bit_1_out_3, eq_4_bit_2_out_3,
       eq_4_bit_3_out_3, eq_4_bit_4_out_3, eq_4_bit_5_out_3, eq_4_bit_6_out_3, eq_4_bit_7_out_3,
       eq_4_bit_8_out_3;

  eq__4_bit eq_4_bit_1 (.in_1(in_1[3:0]), .in_2(in_2[3:0]), .out_3(eq_4_bit_1_out_3));
  eq__4_bit eq_4_bit_2 (.in_1(in_1[7:4]), .in_2(in_2[7:4]), .out_3(eq_4_bit_2_out_3));
  eq__4_bit eq_4_bit_3 (.in_1(in_1[11:8]), .in_2(in_2[11:8]), .out_3(eq_4_bit_3_out_3));
  eq__4_bit eq_4_bit_4 (.in_1(in_1[15:12]), .in_2(in_2[15:12]), .out_3(eq_4_bit_4_out_3));
  eq__4_bit eq_4_bit_5 (.in_1(in_1[19:16]), .in_2(in_2[19:16]), .out_3(eq_4_bit_5_out_3));
  eq__4_bit eq_4_bit_6 (.in_1(in_1[23:20]), .in_2(in_2[23:20]), .out_3(eq_4_bit_6_out_3));
  eq__4_bit eq_4_bit_7 (.in_1(in_1[27:24]), .in_2(in_2[27:24]), .out_3(eq_4_bit_7_out_3));
  eq__4_bit eq_4_bit_8 (.in_1(in_1[31:28]), .in_2(in_2[31:28]), .out_3(eq_4_bit_8_out_3));
  and and_1 (and_1_out, eq_4_bit_1_out_3, eq_4_bit_2_out_3);
  and and_2 (and_2_out, eq_4_bit_3_out_3, eq_4_bit_4_out_3);
  and and_3 (and_3_out, eq_4_bit_5_out_3, eq_4_bit_6_out_3);
  and and_4 (and_4_out, eq_4_bit_7_out_3, eq_4_bit_8_out_3);
  and and_5 (and_5_out, and_1_out, and_2_out);
  and and_6 (out_3, and_5_out, and_7_out);
  and and_7 (and_7_out, and_3_out, and_4_out);
endmodule

module eq_lt_unsigned_unit (
  input  in_1,
  input  in_2,
  input  in_3,
  input  in_4,
  output out_5,
  output out_6
);

  wire and_2_out;

  and and_1 (out_5, in_2, in_3);
  and and_2 (and_2_out, in_1, in_3);
  or or_1 (out_6, and_2_out, in_4);
endmodule

module eq_lt_unsigned__8_bit (
  input  [7:0] Input_1,
  input  [7:0] Input_2,
  output Equal,
  output Less_than
);

  wire and_1_out, and_2_out, and_3_out, and_4_out, and_5_out, and_6_out, and_7_out, and_8_out, and_9_out,
       and_10_out, and_11_out, and_12_out, and_13_out, and_14_out, and_15_out, and_16_out, and_17_out,
       and_18_out, and_19_out, and_20_out, and_21_out, and_22_out, and_23_out, and_24_out, and_25_out,
       and_26_out, and_27_out, and_28_out, and_29_out, and_30_out, and_31_out, and_32_out, and_33_out,
       and_34_out, and_35_out, and_36_out, and_38_out, not_1_out, not_2_out, not_3_out, not_4_out, not_5_out,
       not_6_out, not_7_out, not_8_out, not_9_out, not_10_out, not_11_out, not_12_out, not_13_out,
       not_14_out, not_15_out, not_16_out, not_17_out, not_18_out, not_19_out, not_20_out, not_21_out,
       not_22_out, not_23_out, not_24_out, or_1_out, or_2_out, or_3_out, or_4_out, or_5_out, or_6_out,
       or_7_out, or_8_out, or_9_out, or_10_out, or_11_out, or_12_out, or_13_out, or_14_out;

  and and_1 (and_1_out, Input_1[0], Input_2[0]);
  not not_1 (not_1_out, Input_1[0]);
  not not_2 (not_2_out, Input_2[0]);
  not not_3 (not_3_out, Input_1[0]);
  and and_2 (and_2_out, Input_1[1], Input_2[1]);
  not not_4 (not_4_out, Input_1[1]);
  not not_5 (not_5_out, Input_2[1]);
  not not_6 (not_6_out, Input_1[1]);
  and and_3 (and_3_out, Input_1[2], Input_2[2]);
  not not_7 (not_7_out, Input_1[2]);
  not not_8 (not_8_out, Input_2[2]);
  not not_9 (not_9_out, Input_1[2]);
  and and_4 (and_4_out, Input_1[3], Input_2[3]);
  not not_10 (not_10_out, Input_1[3]);
  not not_11 (not_11_out, Input_2[3]);
  not not_12 (not_12_out, Input_1[3]);
  and and_5 (and_5_out, Input_1[4], Input_2[4]);
  not not_13 (not_13_out, Input_1[4]);
  not not_14 (not_14_out, Input_2[4]);
  not not_15 (not_15_out, Input_1[4]);
  and and_6 (and_6_out, Input_1[5], Input_2[5]);
  not not_16 (not_16_out, Input_1[5]);
  not not_17 (not_17_out, Input_2[5]);
  not not_18 (not_18_out, Input_1[5]);
  and and_7 (and_7_out, Input_1[6], Input_2[6]);
  not not_19 (not_19_out, Input_1[6]);
  not not_20 (not_20_out, Input_2[6]);
  not not_21 (not_21_out, Input_1[6]);
  and and_8 (and_8_out, Input_1[7], Input_2[7]);
  not not_22 (not_22_out, Input_1[7]);
  not not_23 (not_23_out, Input_2[7]);
  not not_24 (not_24_out, Input_1[7]);
  or or_1 (or_1_out, and_1_out, and_9_out);
  and and_9 (and_9_out, not_1_out, not_2_out);
  and and_10 (and_10_out, not_3_out, Input_2[0]);
  or or_2 (or_2_out, and_2_out, and_11_out);
  and and_11 (and_11_out, not_4_out, not_5_out);
  and and_12 (and_12_out, not_6_out, Input_2[1]);
  or or_3 (or_3_out, and_3_out, and_13_out);
  and and_13 (and_13_out, not_7_out, not_8_out);
  and and_14 (and_14_out, not_9_out, Input_2[2]);
  or or_4 (or_4_out, and_4_out, and_15_out);
  and and_15 (and_15_out, not_10_out, not_11_out);
  and and_16 (and_16_out, not_12_out, Input_2[3]);
  or or_5 (or_5_out, and_5_out, and_17_out);
  and and_17 (and_17_out, not_13_out, not_14_out);
  and and_18 (and_18_out, not_15_out, Input_2[4]);
  or or_6 (or_6_out, and_6_out, and_19_out);
  and and_19 (and_19_out, not_16_out, not_17_out);
  and and_20 (and_20_out, not_18_out, Input_2[5]);
  or or_7 (or_7_out, and_7_out, and_21_out);
  and and_21 (and_21_out, not_19_out, not_20_out);
  and and_22 (and_22_out, not_21_out, Input_2[6]);
  or or_8 (or_8_out, and_8_out, and_23_out);
  and and_23 (and_23_out, not_22_out, not_23_out);
  and and_24 (and_24_out, not_24_out, Input_2[7]);
  and and_25 (and_25_out, or_1_out, or_2_out);
  and and_26 (and_26_out, and_10_out, or_2_out);
  and and_27 (and_27_out, or_3_out, or_4_out);
  and and_28 (and_28_out, and_14_out, or_4_out);
  and and_29 (and_29_out, or_5_out, or_6_out);
  and and_30 (and_30_out, and_18_out, or_6_out);
  and and_31 (and_31_out, or_7_out, or_8_out);
  and and_32 (and_32_out, and_22_out, or_8_out);
  or or_9 (or_9_out, and_26_out, and_12_out);
  or or_10 (or_10_out, and_28_out, and_16_out);
  or or_11 (or_11_out, and_30_out, and_20_out);
  or or_12 (or_12_out, and_32_out, and_24_out);
  and and_33 (and_33_out, and_25_out, and_27_out);
  and and_34 (and_34_out, or_9_out, and_27_out);
  or or_13 (or_13_out, and_34_out, or_10_out);
  and and_35 (and_35_out, and_29_out, and_31_out);
  and and_36 (and_36_out, or_11_out, and_31_out);
  or or_14 (or_14_out, and_36_out, or_12_out);
  and and_37 (Equal, and_33_out, and_35_out);
  and and_38 (and_38_out, or_13_out, and_35_out);
  or or_15 (Less_than, and_38_out, or_14_out);
endmodule

module eq_lt_unsigned__32_bit (
  input  [31:0] Input_1,
  input  [31:0] Input_2,
  output Equal,
  output Less_than
);

  wire eq_lt_unsigned_8_bit_1_equal, eq_lt_unsigned_8_bit_1_less_than, eq_lt_unsigned_8_bit_2_equal,
       eq_lt_unsigned_8_bit_2_less_than, eq_lt_unsigned_8_bit_3_equal, eq_lt_unsigned_8_bit_3_less_than,
       eq_lt_unsigned_8_bit_4_equal, eq_lt_unsigned_8_bit_4_less_than, eq_lt_unsigned_unit_1_out_5,
       eq_lt_unsigned_unit_1_out_6, eq_lt_unsigned_unit_2_out_5, eq_lt_unsigned_unit_2_out_6;

  eq_lt_unsigned__8_bit eq_lt_unsigned_8_bit_1 (
    .Input_1(Input_1[7:0]), .Input_2(Input_2[7:0]), .Equal(eq_lt_unsigned_8_bit_1_equal),
    .Less_than(eq_lt_unsigned_8_bit_1_less_than));
  eq_lt_unsigned__8_bit eq_lt_unsigned_8_bit_2 (
    .Input_1(Input_1[15:8]), .Input_2(Input_2[15:8]), .Equal(eq_lt_unsigned_8_bit_2_equal),
    .Less_than(eq_lt_unsigned_8_bit_2_less_than));
  eq_lt_unsigned_unit eq_lt_unsigned_unit_1 (
    .in_3(eq_lt_unsigned_8_bit_2_equal), .in_4(eq_lt_unsigned_8_bit_2_less_than),
    .out_5(eq_lt_unsigned_unit_1_out_5), .out_6(eq_lt_unsigned_unit_1_out_6),
    .in_1(eq_lt_unsigned_8_bit_1_less_than), .in_2(eq_lt_unsigned_8_bit_1_equal));
  eq_lt_unsigned__8_bit eq_lt_unsigned_8_bit_3 (
    .Input_1(Input_1[23:16]), .Input_2(Input_2[23:16]), .Equal(eq_lt_unsigned_8_bit_3_equal),
    .Less_than(eq_lt_unsigned_8_bit_3_less_than));
  eq_lt_unsigned__8_bit eq_lt_unsigned_8_bit_4 (
    .Input_1(Input_1[31:24]), .Input_2(Input_2[31:24]), .Equal(eq_lt_unsigned_8_bit_4_equal),
    .Less_than(eq_lt_unsigned_8_bit_4_less_than));
  eq_lt_unsigned_unit eq_lt_unsigned_unit_2 (
    .in_3(eq_lt_unsigned_8_bit_4_equal), .in_4(eq_lt_unsigned_8_bit_4_less_than),
    .out_5(eq_lt_unsigned_unit_2_out_5), .out_6(eq_lt_unsigned_unit_2_out_6),
    .in_1(eq_lt_unsigned_8_bit_3_less_than), .in_2(eq_lt_unsigned_8_bit_3_equal));
  eq_lt_unsigned_unit eq_lt_unsigned_unit_3 (
    .in_3(eq_lt_unsigned_unit_2_out_5), .in_4(eq_lt_unsigned_unit_2_out_6), .out_5(Equal), .out_6(Less_than),
    .in_1(eq_lt_unsigned_unit_1_out_6), .in_2(eq_lt_unsigned_unit_1_out_5));
endmodule

module eq_lt_signed__8_bit (
  input  [7:0] Input_1,
  input  [7:0] Input_2,
  output Equal,
  output Less_than
);

  eq_lt_unsigned__8_bit eq_lt_unsigned_8_bit_1 (
    .Input_1({Input_2[7], Input_1[6:0]}), .Input_2({Input_1[7], Input_2[6:0]}), .Equal(Equal),
    .Less_than(Less_than));
endmodule

module eq_lt_signed__32_bit (
  input  [31:0] Input_1,
  input  [31:0] Input_2,
  output Equal,
  output Less_than
);

  eq_lt_unsigned__32_bit eq_lt_unsigned_32_bit_1 (
    .Input_1({Input_2[31], Input_1[30:0]}), .Input_2({Input_1[31], Input_2[30:0]}), .Less_than(Less_than),
    .Equal(Equal));
endmodule

module shiftl__8_bit (
  input  [7:0] in_1,
  output [7:0] out_2
);


  assign out_2 = {in_1[6:0], 1'b0};
endmodule

module shiftl__32_bit (
  input  [31:0] in_1,
  output [31:0] out_2
);


  assign out_2 = {in_1[30:0], 1'b0};
endmodule

module shiftr__8_bit (
  input  [7:0] in_1,
  input  in_2,
  output [7:0] out_3
);


  assign out_3 = {in_2, in_1[7:1]};
endmodule

module shiftr__32_bit (
  input  [31:0] in_1,
  input  in_2,
  output [31:0] out_3
);

  and and_1 (out_3[31], in_1[31], in_2);

  assign out_3[30:0] = in_1[31:1];
endmodule

module shiftl_variable__32_bit (
  input  [31:0] in_1,
  input  [4:0] in_2,
  output [31:0] out_3
);

  wire [31:1] multiplexer_4_out;
  wire [31:2] multiplexer_3_out;
  wire [31:4] multiplexer_2_out;
  wire [31:8] multiplexer_1_out;
  wire [31:24] multiplexer_1_out_2;
  wire [31:28] multiplexer_2_out_2;
  wire [31:30] multiplexer_3_out_2;
  wire [31:31] multiplexer_4_out_2;

  Multiplexer #(.width(32), .enable("false")) multiplexer_1 (
    .in0(in_1), .in1({in_1[15:0], {16{1'b0}}}), .out({multiplexer_1_out_2, multiplexer_1_out}), .sel(in_2[4]));
  Multiplexer #(.width(32), .enable("false")) multiplexer_2 (
    .in0({multiplexer_1_out_2, multiplexer_1_out}), .in1({multiplexer_1_out, {8{1'b0}}}),
    .out({multiplexer_2_out_2, multiplexer_2_out}), .sel(in_2[3]));
  Multiplexer #(.width(32), .enable("false")) multiplexer_3 (
    .in0({multiplexer_2_out_2, multiplexer_2_out}), .in1({multiplexer_2_out, 4'b0000}),
    .out({multiplexer_3_out_2, multiplexer_3_out}), .sel(in_2[2]));
  Multiplexer #(.width(32), .enable("false")) multiplexer_4 (
    .in0({multiplexer_3_out_2, multiplexer_3_out}), .in1({multiplexer_3_out, 2'b00}),
    .out({multiplexer_4_out_2[31], multiplexer_4_out}), .sel(in_2[1]));
  Multiplexer #(.width(32), .enable("false")) multiplexer_5 (
    .in0({multiplexer_4_out_2[31], multiplexer_4_out}), .in1({multiplexer_4_out, 1'b0}), .out(out_3),
    .sel(in_2[0]));
endmodule

module shiftr_variable__32_bit (
  input  [31:0] in_1,
  input  [4:0] in_2,
  input  in_3,
  output [31:0] out_4
);

  wire [0:0] multiplexer_4_out_2;
  wire [3:0] multiplexer_2_out_2;
  wire [27:0] multiplexer_2_out;
  wire [30:0] multiplexer_4_out;
  wire [31:0] multiplexer_1_out, multiplexer_3_out;
  wire [31:31] and_1_out;

  and and_1 (and_1_out[31], in_1[31], in_3);
  Multiplexer #(.width(32), .enable("false")) multiplexer_1 (
    .in0(in_1), .in1({{16{and_1_out[31]}}, in_1[31:16]}), .out(multiplexer_1_out), .sel(in_2[4]));
  Multiplexer #(.width(32), .enable("false")) multiplexer_2 (
    .in0(multiplexer_1_out), .in1({{8{and_1_out[31]}}, multiplexer_1_out[31:8]}),
    .out({multiplexer_2_out, multiplexer_2_out_2}), .sel(in_2[3]));
  Multiplexer #(.width(32), .enable("false")) multiplexer_3 (
    .in0({multiplexer_2_out, multiplexer_2_out_2}), .in1({{4{and_1_out[31]}}, multiplexer_2_out}),
    .out(multiplexer_3_out), .sel(in_2[2]));
  Multiplexer #(.width(32), .enable("false")) multiplexer_4 (
    .in0(multiplexer_3_out), .in1({{2{and_1_out[31]}}, multiplexer_3_out[31:2]}),
    .out({multiplexer_4_out, multiplexer_4_out_2[0]}), .sel(in_2[1]));
  Multiplexer #(.width(32), .enable("false")) multiplexer_5 (
    .in0({multiplexer_4_out, multiplexer_4_out_2[0]}), .in1({and_1_out[31], multiplexer_4_out}), .out(out_4),
    .sel(in_2[0]));
endmodule
