// Logisim project IE4756-fast-adder.circ as structural Verilog: 2 circuits, main circuit main
module main (
  input  [31:0] in_1,
  input  [31:0] in_2,
  output [31:0] out_3
);

  add_32 add_32_1 (.in_1(in_1), .in_2(in_2), .out_4(out_3), .in_3(1'b0));  // open: out_5, out_6
endmodule

module add_32 (
  input  [31:0] in_1,
  input  [31:0] in_2,
  input  in_3,
  output [31:0] out_4,
  output out_5,
  output out_6
);

  Adder #(.width(32)) adder_1 (.a(in_1), .b(in_2), .out(out_4), .cout(in_3));  // open: cin

  assign out_6 = 1'b0;
endmodule
